// Logisim project M4_8.1.circ as structural Verilog: 1 circuit, main circuit main
module main (
);

  wire ABUS, ABUSHL, ABUSPC, ABUSSP, ABUST, ALUEN, and_2_out, and_3_out, and_8_out, and_9_out, and_10_out, C,
       CLK, clock_1_out, comparator_1_eq, comparator_2_eq, COUT, d_ff_2_qn, DBUSA, DBUSALU, DBUSB, DBUSH,
       DBUSL, DBUSPCH, DBUSPCL, DBUSS, DBUSSPH, DBUSSPL, DBUSTL, demultiplexer_1_out1, DREAD, DWRITE, HALT,
       LOADA, LOADB, LOADH, LOADL, LOADPC, LOADSPH, LOADSPL, LOADTH, LOADTL, nor_1_out, nor_2_out, nor_3_out,
       nor_4_out, not_1_out, not_3_out, nPOR, NXTI, or_1_out, or_2_out, or_3_out, PCINC, PH0, POR, por_1_out,
       RAMREAD, RAMWRITE, RUN, RUNNING, SPL_carry, SPOP, SPUP, SS, STOP, Z;
  wire [0:0] ALUL_data_2;
  wire [1:1] and_1_out;
  wire [2:0] ALUOP, PH;
  wire [3:0] bit_extender_2_out;
  wire [7:0] A, ALUL_data, B, BOOTROM_data, controlled_buffer_7_out, DATA, H_q, IR, L_q, TL_q;
  wire [15:0] AD, PC, SP;
  wire [15:8] PCDATA16;
  wire [23:0] bit_extender_1_out, IDECODE_data;
  wire [23:3] and_5_out;

  Clock clock_1 (.out(clock_1_out));
  or or_1 (or_1_out, POR, STOP, HALT);
  or or_2 (or_2_out, PH0, PCINC);
  POR #(.PorHighDuration(1), .porsize(1)) por_1 (.out(por_1_out));
  and and_1 (and_1_out[1], clock_1_out, nPOR);
  nor nor_1 (nor_1_out, RUN, nor_2_out);
  nor nor_2 (nor_2_out, nor_1_out, or_1_out);
  Counter #(.max('hffff), .width(16)) u_PC (
    .clr(POR), .load(LOADPC), .count(or_2_out), .clk(CLK), .D({PCDATA16, DATA}), .Q(PC));  // open: up, carry
  D_Flip_Flop d_ff_1 (.D(nor_2_out), .clk(clock_1_out), .Q(RUNNING));  // open: Qn, preset, reset
  Counter SPL (.clr(POR), .load(LOADSPL), .up(SPUP), .count(SPOP), .clk(CLK), .D(DATA), .carry(SPL_carry), .Q(SP[7:0]));
  nor nor_3 (nor_3_out, AD[15], AD[14], AD[13], AD[12], AD[11], AD[10]);
  ROM #(.addrWidth(10)) BOOTROM (.addr(AD[9:0]), .data(BOOTROM_data));
  D_Flip_Flop #(.trigger("falling")) d_ff_2 (
    .D(not_1_out), .clk(clock_1_out), .Qn(d_ff_2_qn));  // open: Q, preset, reset
  not not_1 (not_1_out, por_1_out);
  BitSelector #(.width(2)) bitselector_1 (.in({and_1_out[1], SS}), .out(CLK), .sel(RUNNING));
  Counter #(.max('h7), .width(3)) PHASECOUNTER (
    .clr(POR), .load(NXTI), .clk(CLK), .D(3'b000), .Q(PH));  // open: up, count, carry
  assign AD = or_3_out ? PC : 16'bz;  // Controlled_Buffer controlled_buffer_1
  or or_3 (or_3_out, PH0, ABUSPC);
  or or_4 (POR, por_1_out, d_ff_2_qn);
  assign DATA = DBUSPCL ? PC[7:0] : 8'bz;  // Controlled_Buffer controlled_buffer_2
  assign DATA = DBUSPCH ? PC[15:8] : 8'bz;  // Controlled_Buffer controlled_buffer_3
  and and_2 (and_2_out, SPOP, SPL_carry);
  not not_2 (nPOR, POR);
  Counter counter_1 (
    .clr(POR), .load(LOADSPH), .up(SPUP), .count(and_2_out), .clk(CLK), .D(DATA), .Q(SP[15:8]));  // open: carry
  and and_3 (and_3_out, nor_3_out, DREAD);
  assign DATA = and_3_out ? BOOTROM_data : 8'bz;  // Controlled_Buffer controlled_buffer_4
  nor nor_4 (nor_4_out, PH[0], PH[1], PH[2]);
  ROM #(.addrWidth(11), .dataWidth(24)) IDECODE (.addr({IR, PH}), .data(IDECODE_data));
  and and_4 (PH0, nPOR, nor_4_out);
  RAM #(.addrWidth(10), .asyncread("true"), .databus("bidir"), .\type ("nonvolatile")) ram_1 (
    .addr(AD[9:0]), .we(RAMWRITE), .oe(RAMREAD), .clk(CLK));  // open: data
  LED led_1 (.in(RUNNING));
  LED led_2 (.in(POR));
  assign AD = ABUSSP ? SP : 16'bz;  // Controlled_Buffer controlled_buffer_5
  Comparator #(.width(6)) comparator_1 (.a({6{1'b1}}), .b(AD[15:10]), .eq(comparator_1_eq));  // open: gt, lt
  LED led_3 (.in(CLK));
  Hex_Digit_Display hex_digit_display_1 (.value(PC[15:12]));  // open: dp
  Button button_1 (.out(RUN));
  assign bit_extender_1_out = {{23{PH0}}, PH0};  // Bit_Extender bit_extender_1
  Hex_Digit_Display hex_digit_display_2 (.value(PC[11:8]));  // open: dp
  Hex_Digit_Display hex_digit_display_3 (.value(PC[7:4]));  // open: dp
  Button button_2 (.out(STOP));
  assign {and_5_out[23:17], ALUEN, SPUP, SPOP, ABUS, PCINC, NXTI, and_5_out[10:3], ALUOP} = IDECODE_data & ~bit_extender_1_out;  // AND_Gate and_5, 24 bits wide
  and and_6 (RAMREAD, DREAD, comparator_1_eq);
  and and_7 (RAMWRITE, comparator_1_eq, DWRITE);
  Hex_Digit_Display hex_digit_display_4 (.value(PC[3:0]));  // open: dp
  Button button_3 (.out(SS));
  Register u_IR (.D(DATA), .en(PH0), .clk(CLK), .Q(IR), .clr(POR));
  assign DATA = RAMREAD ? controlled_buffer_7_out : 8'bz;  // Controlled_Buffer controlled_buffer_6
  assign controlled_buffer_7_out = RAMWRITE ? DATA : 8'bz;  // Controlled_Buffer controlled_buffer_7
  Hex_Digit_Display hex_digit_display_5 (.value(IR[7:4]));  // open: dp
  Hex_Digit_Display hex_digit_display_6 (.value(IR[3:0]));  // open: dp
  Hex_Digit_Display hex_digit_display_7 (.value(bit_extender_2_out));  // open: dp
  assign bit_extender_2_out = {{1{1'b0}}, PH};  // Bit_Extender bit_extender_2
  Hex_Digit_Display hex_digit_display_8 (.value(DATA[7:4]));  // open: dp
  Hex_Digit_Display hex_digit_display_9 (.value(DATA[3:0]));  // open: dp
  not not_3 (not_3_out, PH0);
  Register u_A (.D(DATA), .en(LOADA), .clk(CLK), .Q(A));  // open: clr
  Register u_B (.D(DATA), .en(LOADB), .clk(CLK), .Q(B));  // open: clr
  Register H (.D(DATA), .en(LOADH), .clk(CLK), .Q(H_q));  // open: clr
  Register L (.D(DATA), .en(LOADL), .clk(CLK), .Q(L_q));  // open: clr
  Register TL (.D(DATA), .en(LOADTL), .clk(CLK), .Q(TL_q));  // open: clr
  Register TH (.D(DATA), .en(LOADTH), .clk(CLK), .Q(PCDATA16));  // open: clr
  Demultiplexer #(.select(4)) demultiplexer_1 (
    .out1(demultiplexer_1_out1), .out2(DBUSPCH), .out3(DBUSPCL), .out4(DBUSSPH), .out5(DBUSSPL),
    .out6(DBUSTL), .out7(DBUSA), .out8(DBUSB), .out9(DBUSH), .out10(DBUSL), .out11(DBUSS), .out12(DBUSALU),
    .in(not_3_out), .sel(and_5_out[10:7]));  // open: out0, out13, out14, out15
  and and_8 (and_8_out, ABUS, not_3_out);
  Demultiplexer #(.select(3)) demultiplexer_2 (
    .out1(ABUSPC), .out2(ABUSSP), .out3(ABUSHL), .out4(ABUST), .out5(HALT), .in(and_8_out), .sel(ALUOP));  // open: out0, out6, out7
  assign DATA = DBUSA ? A : 8'bz;  // Controlled_Buffer controlled_buffer_8
  assign DATA = DBUSB ? B : 8'bz;  // Controlled_Buffer controlled_buffer_9
  assign DATA = DBUSH ? H_q : 8'bz;  // Controlled_Buffer controlled_buffer_10
  assign AD = ABUSHL ? {H_q, L_q} : 16'bz;  // Controlled_Buffer controlled_buffer_11
  assign DATA = DBUSL ? L_q : 8'bz;  // Controlled_Buffer controlled_buffer_12
  assign DATA = DBUSTL ? TL_q : 8'bz;  // Controlled_Buffer controlled_buffer_13
  TTY tty_1 (.data(DATA[6:0]), .clk(CLK), .we(and_9_out));  // open: clr
  assign AD = ABUST ? {PCDATA16, TL_q} : 16'bz;  // Controlled_Buffer controlled_buffer_14
  or or_5 (DREAD, PH0, demultiplexer_1_out1);
  and and_9 (and_9_out, comparator_2_eq, DWRITE);
  Comparator #(.width(16)) comparator_2 (.a(16'h400), .b(AD), .eq(comparator_2_eq));  // open: gt, lt
  Demultiplexer #(.select(4)) demultiplexer_3 (
    .out1(DWRITE), .out2(LOADPC), .out3(LOADSPH), .out4(LOADSPL), .out5(LOADTH), .out6(LOADTL), .out7(LOADA),
    .out8(LOADB), .out9(LOADH), .out10(LOADL), .in(not_3_out), .sel(and_5_out[6:3]));  // open: out0, out11, out12, out13, out14, out15
  Register #(.width(1)) u_C (.D(COUT), .en(ALUEN), .clk(CLK), .Q(C));  // open: clr
  ROM #(.addrWidth(12), .dataWidth(5)) ALUL (
    .addr({ALUOP, B[3:0], A[3:0], C}), .data({ALUL_data_2[0], ALUL_data[3:0]}));
  ROM #(.addrWidth(12), .dataWidth(5)) ALUH (
    .addr({ALUOP, B[7:4], A[7:4], ALUL_data_2[0]}), .data({COUT, ALUL_data[7:4]}));
  assign DATA = DBUSS ? {{6{1'b0}}, C, Z} : 8'bz;  // Controlled_Buffer controlled_buffer_15
  and and_10 (and_10_out, ALUL_data[7], ALUL_data[6], ALUL_data[5], ALUL_data[4], ALUL_data[3], ALUL_data[2], ALUL_data[1], ALUL_data[0]);
  Register #(.width(1)) u_Z (.D(and_10_out), .en(ALUEN), .clk(CLK), .Q(Z));  // open: clr
  assign DATA = DBUSALU ? ALUL_data : 8'bz;  // Controlled_Buffer controlled_buffer_16

  // Other names for the same wires on the sheet: PCDATA16[7:0] = DATA

  // Notes on the sheet:
  //   contents of BOOTROM (hex, n*v repeats v):
  //   fe 8 48 10 4 0 8 65 10 4 0 8 6c 10 4 0 8 6c 10 4 0 8 6f 10 4 0 8 72 10 4 0 8 6c 10 4 0 8 64 10 4 0
  //   80 0 1
  //   contents of IDECODE (hex, n*v repeats v):
  //   0 30a9 30b1 28bc 5*0 30a9 30b1 28c4 5*0 30a9 30b1 28cc 5*0 30a9 30b1 28d4 5*0 28bb 7*0 28c3 23*0
  //   38b9 7*0 38c1 7*0 38c9 7*0 38d1 39*0 30a9 30b1 2b8c 5*0 30a9 30b1 2c0c 5*0 30a9 30b1 2c8c 5*0 30a9
  //   30b1 2d0c 5*0 2b8b 7*0 2c0b 87*0 3099 38a1 382*0 bc0 7*0 c38 7*0 430 3c0 b38 365*0 30a9 2891 6*0
  //   30a9 30b1 610a 618a b10 0 0 0 c000 e0b2 20aa b10 988*0 800 7*0 2805
  //   RUN
  //   RST
  //   CLK
  //   PC
  //   IR
  //   PH
  //   contents of ALUL (hex, n*v repeats v):
  //   0 1 1 2 2 3 3 4 4 5 5 6 6 7 7 8 8 9 9 a a b b c c d d e e f f 10 1 2 2 3 3 4 4 5 5 6 6 7 7 8 8 9 9 a
  //   a b b c c d d e e f f 10 10 11 2 3 3 4 4 5 5 6 6 7 7 8 8 9 9 a a b b c c d d e e f f 10 10 11 11 12
  //   3 4 4 5 5 6 6 7 7 8 8 9 9 a a b b c c d d e e f f 10 10 11 11 12 12 13 4 5 5 6 6 7 7 8 8 9 9 a a b b
  //   c c d d e e f f 10 10 11 11 12 12 13 13 14 5 6 6 7 7 8 8 9 9 a a b b c c d d e e f f 10 10 11 11 12
  //   12 13 13 14 14 15 6 7 7 8 8 9 9 a a b b c c d d e e f f 10 10 11 11 12 12 13 13 14 14 15 15 16 7 8 8
  //   9 9 a a b b c c d d e e f f 10 10 11 11 12 12 13 13 14 14 15 15 16 16 17 8 9 9 a a b b c c d d e e f
  //   f 10 10 11 11 12 12 13 13 14 14 15 15 16 16 17 17 18 9 a a b b c c d d e e f f 10 10 11 11 12 12 13
  //   13 14 14 15 15 16 16 17 17 18 18 19 a b b c c d d e e f f 10 10 11 11 12 12 13 13 14 14 15 15 16 16
  //   17 17 18 18 19 19 1a b c c d d e e f f 10 10 11 11 12 12 13 13 14 14 15 15 16 16 17 17 18 18 19 19
  //   1a 1a 1b c d d e e f f 10 10 11 11 12 12 13 13 14 14 15 15 16 16 17 17 18 18 19 19 1a 1a 1b 1b 1c d
  //   e e f f 10 10 11 11 12 12 13 13 14 14 15 15 16 16 17 17 18 18 19 19 1a 1a 1b 1b 1c 1c 1d e f f 10 10
  //   11 11 12 12 13 13 14 14 15 15 16 16 17 17 18 18 19 19 1a 1a 1b 1b 1c 1c 1d 1d 1e f 10 10 11 11 12 12
  //   13 13 14 14 15 15 16 16 17 17 18 18 19 19 1a 1a 1b 1b 1c 1c 1d 1d 1e 1e 1f 0 1f 1f 1e 1e 1d 1d 1c 1c
  //   1b 1b 1a 1a 19 19 18 18 17 17 16 16 15 15 14 14 13 13 12 12 11 11 10 1 0 0 1f 1f 1e 1e 1d 1d 1c 1c
  //   1b 1b 1a 1a 19 19 18 18 17 17 16 16 15 15 14 14 13 13 12 12 11 2 1 1 0 0 1f 1f 1e 1e 1d 1d 1c 1c 1b
  //   1b 1a 1a 19 19 18 18 17 17 16 16 15 15 14 14 13 13 12 3 2 2 1 1 0 0 1f 1f 1e 1e 1d 1d 1c 1c 1b 1b 1a
  //   1a 19 19 18 18 17 17 16 16 15 15 14 14 13 4 3 3 2 2 1 1 0 0 1f 1f 1e 1e 1d 1d 1c 1c 1b 1b 1a 1a 19
  //   19 18 18 17 17 16 16 15 15 14 5 4 4 3 3 2 2 1 1 0 0 1f 1f 1e 1e 1d 1d 1c 1c 1b 1b 1a 1a 19 19 18 18
  //   17 17 16 16 15 6 5 5 4 4 3 3 2 2 1 1 0 0 1f 1f 1e 1e 1d 1d 1c 1c 1b 1b 1a 1a 19 19 18 18 17 17 16 7
  //   6 6 5 5 4 4 3 3 2 2 1 1 0 0 1f 1f 1e 1e 1d 1d 1c 1c 1b 1b 1a 1a 19 19 18 18 17 8 7 7 6 6 5 5 4 4 3 3
  //   2 2 1 1 0 0 1f 1f 1e 1e 1d 1d 1c 1c 1b 1b 1a 1a 19 19 18 9 8 8 7 7 6 6 5 5 4 4 3 3 2 2 1 1 0 0 1f 1f
  //   1e 1e 1d 1d 1c 1c 1b 1b 1a 1a 19 a 9 9 8 8 7 7 6 6 5 5 4 4 3 3 2 2 1 1 0 0 1f 1f 1e 1e 1d 1d 1c 1c
  //   1b 1b 1a b a a 9 9 8 8 7 7 6 6 5 5 4 4 3 3 2 2 1 1 0 0 1f 1f 1e 1e 1d 1d 1c 1c 1b c b b a a 9 9 8 8
  //   7 7 6 6 5 5 4 4 3 3 2 2 1 1 0 0 1f 1f 1e 1e 1d 1d 1c d c c b b a a 9 9 8 8 7 7 6 6 5 5 4 4 3 3 2 2 1
  //   1 0 0 1f 1f 1e 1e 1d e d d c c b b a a 9 9 8 8 7 7 6 6 5 5 4 4 3 3 2 2 1 1 0 0 1f 1f 1e f e e d d c
  //   c b b a a 9 9 8 8 7 7 6 6 5 5 4 4 3 3 2 2 1 1 0 0 1f 34*0 1 1 0 0 1 1 0 0 1 1 0 0 1 1 0 0 1 1 0 0 1
  //   1 0 0 1 1 0 0 1 1 4*0 4*2 4*0 4*2 4*0 4*2 4*0 4*2 0 0 1 1 2 2 3 3 0 0 1 1 2 2 3 3 0 0 1 1 2 2 3 3 0
  //   0 1 1 2 2 3 3 8*0 8*4 8*0 8*4 0 0 1 1 0 0 1 1 4 4 5 5 4 4 5 5 0 0 1 1 0 0 1 1 4 4 5 5 4 4 5 5 4*0
  //   4*2 4*4 4*6 4*0 4*2 4*4 4*6 0 0 1 1 2 2 3 3 4 4 5 5 6 6 7 7 0 0 1 1 2 2 3 3 4 4 5 5 6 6 7 7 16*0
  //   16*8 0 0 1 1 0 0 1 1 0 0 1 1 0 0 1 1 8 8 9 9 8 8 9 9 8 8 9 9 8 8 9 9 4*0 4*2 4*0 4*2 4*8 4*a 4*8 4*a
  //   0 0 1 1 2 2 3 3 0 0 1 1 2 2 3 3 8 8 9 9 a a b b 8 8 9 9 a a b b 8*0 8*4 8*8 8*c 0 0 1 1 0 0 1 1 4 4
  //   5 5 4 4 5 5 8 8 9 9 8 8 9 9 c c d d c c d d 4*0 4*2 4*4 4*6 4*8 4*a 4*c 4*e 0 0 1 1 2 2 3 3 4 4 5 5
  //   6 6 7 7 8 8 9 9 a a b b c c d d e e f f 0 0 1 1 2 2 3 3 4 4 5 5 6 6 7 7 8 8 9 9 a a b b c c d d e e
  //   f f 4*1 4*3 4*5 4*7 4*9 4*b 4*d 4*f 2 2 3 3 2 2 3 3 6 6 7 7 6 6 7 7 a a b b a a b b e e f f e e f f
  //   8*3 8*7 8*b 8*f 4 4 5 5 6 6 7 7 4 4 5 5 6 6 7 7 c c d d e e f f c c d d e e f f 4*5 4*7 4*5 4*7 4*d
  //   4*f 4*d 4*f 6 6 7 7 6 6 7 7 6 6 7 7 6 6 7 7 e e f f e e f f e e f f e e f f 16*7 16*f 8 8 9 9 a a b
  //   b c c d d e e f f 8 8 9 9 a a b b c c d d e e f f 4*9 4*b 4*d 4*f 4*9 4*b 4*d 4*f a a b b a a b b e
  //   e f f e e f f a a b b a a b b e e f f e e f f 8*b 8*f 8*b 8*f c c d d e e f f c c d d e e f f c c d
  //   d e e f f c c d d e e f f 4*d 4*f 4*d 4*f 4*d 4*f 4*d 4*f e e f f e e f f e e f f e e f f e e f f e
  //   e f f e e f f e e 34*f 0 0 1 1 2 2 3 3 4 4 5 5 6 6 7 7 8 8 9 9 a a b b c c d d e e f f 1 1 0 0 3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
  //   contents of ALUH (hex, n*v repeats v):
  //   0 1 1 2 2 3 3 4 4 5 5 6 6 7 7 8 8 9 9 a a b b c c d d e e f f 10 1 2 2 3 3 4 4 5 5 6 6 7 7 8 8 9 9 a
  //   a b b c c d d e e f f 10 10 11 2 3 3 4 4 5 5 6 6 7 7 8 8 9 9 a a b b c c d d e e f f 10 10 11 11 12
  //   3 4 4 5 5 6 6 7 7 8 8 9 9 a a b b c c d d e e f f 10 10 11 11 12 12 13 4 5 5 6 6 7 7 8 8 9 9 a a b b
  //   c c d d e e f f 10 10 11 11 12 12 13 13 14 5 6 6 7 7 8 8 9 9 a a b b c c d d e e f f 10 10 11 11 12
  //   12 13 13 14 14 15 6 7 7 8 8 9 9 a a b b c c d d e e f f 10 10 11 11 12 12 13 13 14 14 15 15 16 7 8 8
  //   9 9 a a b b c c d d e e f f 10 10 11 11 12 12 13 13 14 14 15 15 16 16 17 8 9 9 a a b b c c d d e e f
  //   f 10 10 11 11 12 12 13 13 14 14 15 15 16 16 17 17 18 9 a a b b c c d d e e f f 10 10 11 11 12 12 13
  //   13 14 14 15 15 16 16 17 17 18 18 19 a b b c c d d e e f f 10 10 11 11 12 12 13 13 14 14 15 15 16 16
  //   17 17 18 18 19 19 1a b c c d d e e f f 10 10 11 11 12 12 13 13 14 14 15 15 16 16 17 17 18 18 19 19
  //   1a 1a 1b c d d e e f f 10 10 11 11 12 12 13 13 14 14 15 15 16 16 17 17 18 18 19 19 1a 1a 1b 1b 1c d
  //   e e f f 10 10 11 11 12 12 13 13 14 14 15 15 16 16 17 17 18 18 19 19 1a 1a 1b 1b 1c 1c 1d e f f 10 10
  //   11 11 12 12 13 13 14 14 15 15 16 16 17 17 18 18 19 19 1a 1a 1b 1b 1c 1c 1d 1d 1e f 10 10 11 11 12 12
  //   13 13 14 14 15 15 16 16 17 17 18 18 19 19 1a 1a 1b 1b 1c 1c 1d 1d 1e 1e 1f 0 1f 1f 1e 1e 1d 1d 1c 1c
  //   1b 1b 1a 1a 19 19 18 18 17 17 16 16 15 15 14 14 13 13 12 12 11 11 10 1 0 0 1f 1f 1e 1e 1d 1d 1c 1c
  //   1b 1b 1a 1a 19 19 18 18 17 17 16 16 15 15 14 14 13 13 12 12 11 2 1 1 0 0 1f 1f 1e 1e 1d 1d 1c 1c 1b
  //   1b 1a 1a 19 19 18 18 17 17 16 16 15 15 14 14 13 13 12 3 2 2 1 1 0 0 1f 1f 1e 1e 1d 1d 1c 1c 1b 1b 1a
  //   1a 19 19 18 18 17 17 16 16 15 15 14 14 13 4 3 3 2 2 1 1 0 0 1f 1f 1e 1e 1d 1d 1c 1c 1b 1b 1a 1a 19
  //   19 18 18 17 17 16 16 15 15 14 5 4 4 3 3 2 2 1 1 0 0 1f 1f 1e 1e 1d 1d 1c 1c 1b 1b 1a 1a 19 19 18 18
  //   17 17 16 16 15 6 5 5 4 4 3 3 2 2 1 1 0 0 1f 1f 1e 1e 1d 1d 1c 1c 1b 1b 1a 1a 19 19 18 18 17 17 16 7
  //   6 6 5 5 4 4 3 3 2 2 1 1 0 0 1f 1f 1e 1e 1d 1d 1c 1c 1b 1b 1a 1a 19 19 18 18 17 8 7 7 6 6 5 5 4 4 3 3
  //   2 2 1 1 0 0 1f 1f 1e 1e 1d 1d 1c 1c 1b 1b 1a 1a 19 19 18 9 8 8 7 7 6 6 5 5 4 4 3 3 2 2 1 1 0 0 1f 1f
  //   1e 1e 1d 1d 1c 1c 1b 1b 1a 1a 19 a 9 9 8 8 7 7 6 6 5 5 4 4 3 3 2 2 1 1 0 0 1f 1f 1e 1e 1d 1d 1c 1c
  //   1b 1b 1a b a a 9 9 8 8 7 7 6 6 5 5 4 4 3 3 2 2 1 1 0 0 1f 1f 1e 1e 1d 1d 1c 1c 1b c b b a a 9 9 8 8
  //   7 7 6 6 5 5 4 4 3 3 2 2 1 1 0 0 1f 1f 1e 1e 1d 1d 1c d c c b b a a 9 9 8 8 7 7 6 6 5 5 4 4 3 3 2 2 1
  //   1 0 0 1f 1f 1e 1e 1d e d d c c b b a a 9 9 8 8 7 7 6 6 5 5 4 4 3 3 2 2 1 1 0 0 1f 1f 1e f e e d d c
  //   c b b a a 9 9 8 8 7 7 6 6 5 5 4 4 3 3 2 2 1 1 0 0 1f 34*0 1 1 0 0 1 1 0 0 1 1 0 0 1 1 0 0 1 1 0 0 1
  //   1 0 0 1 1 0 0 1 1 4*0 4*2 4*0 4*2 4*0 4*2 4*0 4*2 0 0 1 1 2 2 3 3 0 0 1 1 2 2 3 3 0 0 1 1 2 2 3 3 0
  //   0 1 1 2 2 3 3 8*0 8*4 8*0 8*4 0 0 1 1 0 0 1 1 4 4 5 5 4 4 5 5 0 0 1 1 0 0 1 1 4 4 5 5 4 4 5 5 4*0
  //   4*2 4*4 4*6 4*0 4*2 4*4 4*6 0 0 1 1 2 2 3 3 4 4 5 5 6 6 7 7 0 0 1 1 2 2 3 3 4 4 5 5 6 6 7 7 16*0
  //   16*8 0 0 1 1 0 0 1 1 0 0 1 1 0 0 1 1 8 8 9 9 8 8 9 9 8 8 9 9 8 8 9 9 4*0 4*2 4*0 4*2 4*8 4*a 4*8 4*a
  //   0 0 1 1 2 2 3 3 0 0 1 1 2 2 3 3 8 8 9 9 a a b b 8 8 9 9 a a b b 8*0 8*4 8*8 8*c 0 0 1 1 0 0 1 1 4 4
  //   5 5 4 4 5 5 8 8 9 9 8 8 9 9 c c d d c c d d 4*0 4*2 4*4 4*6 4*8 4*a 4*c 4*e 0 0 1 1 2 2 3 3 4 4 5 5
  //   6 6 7 7 8 8 9 9 a a b b c c d d e e f f 0 0 1 1 2 2 3 3 4 4 5 5 6 6 7 7 8 8 9 9 a a b b c c d d e e
  //   f f 4*1 4*3 4*5 4*7 4*9 4*b 4*d 4*f 2 2 3 3 2 2 3 3 6 6 7 7 6 6 7 7 a a b b a a b b e e f f e e f f
  //   8*3 8*7 8*b 8*f 4 4 5 5 6 6 7 7 4 4 5 5 6 6 7 7 c c d d e e f f c c d d e e f f 4*5 4*7 4*5 4*7 4*d
  //   4*f 4*d 4*f 6 6 7 7 6 6 7 7 6 6 7 7 6 6 7 7 e e f f e e f f e e f f e e f f 16*7 16*f 8 8 9 9 a a b
  //   b c c d d e e f f 8 8 9 9 a a b b c c d d e e f f 4*9 4*b 4*d 4*f 4*9 4*b 4*d 4*f a a b b a a b b e
  //   e f f e e f f a a b b a a b b e e f f e e f f 8*b 8*f 8*b 8*f c c d d e e f f c c d d e e f f c c d
  //   d e e f f c c d d e e f f 4*d 4*f 4*d 4*f 4*d 4*f 4*d 4*f e e f f e e f f e e f f e e f f e e f f e
  //   e f f e e f f e e 34*f 0 0 1 1 2 2 3 3 4 4 5 5 6 6 7 7 8 8 9 9 a a b b c c d d e e f f 1 1 0 0 3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
endmodule
